# Fritzing sketch Flaps Controller Wiring (saved by Fritzing 0.9.6b)
breadboards: 1

parts:
  Part1 = Arduino Uno (Rev3)
  R1 = Rotary Potentiometer (Small) [maximum_resistance=100kΩ package=THT]
  Min = Pushbutton [package="[THT]"]
  Max = Pushbutton [package="[THT]"]

nets:
  N1: Part1.A0, R1.wiper
  N2: Part1.GND, R1.leg1
  N3: Part1.D2, Min.Pin_3, Min.Pin_4
  N4: Part1.D3_PWM, Max.Pin_3, Max.Pin_4
  N5: Part1.3V3, R1.leg2, Min.Pin_1, Min.Pin_2, Max.Pin_1, Max.Pin_2
